# Fritzing sketch Layout_Breadboard (saved by Fritzing 0.9.10b)
circuit board: 8.46667cm x 5.64444cm
breadboards: 1

parts:
  Arduino_RP2040_Connect = Arduino Nano (Rev3.0)
  S1 = Pushbutton [package="[THT]"]
  SD-Card_Holder = Adafruit SDIO microSD Breakout

nets:
  GND: Arduino_RP2040_Connect.GND, S1.Pin_3, S1.Pin_4, SD-Card_Holder.GND
  N1: Arduino_RP2040_Connect.D4, S1.Pin_1, S1.Pin_2
  N2: Arduino_RP2040_Connect.D10, SD-Card_Holder.CS
  N3: Arduino_RP2040_Connect.D11/MOSI, SD-Card_Holder.DI
  N4: Arduino_RP2040_Connect.D12/MISO, SD-Card_Holder.DO
  3V3: Arduino_RP2040_Connect.3V3, SD-Card_Holder.3.3V
  N5: Arduino_RP2040_Connect.D13/SCK, SD-Card_Holder.SCLK

notes:
  MotoData V 0-1
